// Logisim project ALU.circ as structural Verilog: 1 circuit, main circuit main
module main (
  input  CARRY,
  input  [3:0] CARRY_2,
  input  [3:0] Num_1,
  input  [3:0] Num_2,
  input  Enable,
  input  [2:0] Opcode,
  output [3:0] Output
);

  wire [3:0] adder_1_out, and_1_out, divider_1_out, multiplier_1_out, not_1_out, not_2_out, or_1_out,
       subtractor_1_out;

  Adder #(.width(4)) adder_1 (.a(Num_1), .b(Num_2), .out(adder_1_out), .cin(CARRY));  // open: cout
  Subtractor #(.width(4)) subtractor_1 (.a(Num_1), .b(Num_2), .out(subtractor_1_out), .bin(CARRY));  // open: bout
  Multiplier #(.width(4)) multiplier_1 (.a(Num_1), .b(Num_2), .out(multiplier_1_out), .cin(CARRY_2));  // open: cout
  Divider #(.width(4)) divider_1 (.a(Num_1), .b(Num_2), .out(divider_1_out), .upper(CARRY_2));  // open: rem
  assign and_1_out = Num_2 & Num_1;  // AND_Gate and_1, 4 bits wide
  assign or_1_out = Num_1 | Num_2;  // OR_Gate or_1, 4 bits wide
  assign not_1_out = ~Num_1;  // NOT_Gate not_1, 4 bits wide
  assign not_2_out = ~Num_2;  // NOT_Gate not_2, 4 bits wide
  Multiplexer #(.select(3), .width(4)) multiplexer_1 (
    .in0(adder_1_out), .in1(subtractor_1_out), .in2(multiplier_1_out), .in3(divider_1_out), .in4(and_1_out),
    .in5(or_1_out), .in6(not_1_out), .in7(not_2_out), .out(Output), .sel(Opcode), .en(Enable));

  // Notes on the sheet:
  //   ARITHMETIC AND LOGICAL UNIT (ALU)
  //   Or (101)
  //   Adder (000)
  //   Substractor (001)
  //   Multiplier (010)
  //   Divider (011)
  //   And (100)
  //   Num-1 Not (110)
  //   Num-2 Not (111)
endmodule
