// Logisim project FULL ADDER.circ as structural Verilog: 1 circuit, main circuit main
module main (
  input  A,
  input  B,
  input  Cin,
  output SUM,
  output CARRY
);

  wire and_1_out, and_2_out, xor_1_out;

  xor xor_1 (xor_1_out, A, B);
  and and_1 (and_1_out, A, B);
  and and_2 (and_2_out, xor_1_out, Cin);
  xor xor_2 (SUM, xor_1_out, Cin);
  or or_1 (CARRY, and_1_out, and_2_out);

  // Notes on the sheet:
  //   FULL ADDER
  //   AB
  //   A xor B
  //   (A xor B) Cin
  //   A xor B xor Cin
endmodule
