// Logisim project FULL SUBTRACTOR.circ as structural Verilog: 1 circuit, main circuit main
module main (
  input  A,
  input  B,
  input  C,
  output DIFFERENCE,
  output BORROW
);

  wire and_1_out, and_2_out, not_1_out, not_2_out, xor_1_out;

  not not_1 (not_1_out, A);
  xor xor_1 (xor_1_out, A, B);
  not not_2 (not_2_out, xor_1_out);
  and and_1 (and_1_out, not_2_out, C);
  and and_2 (and_2_out, not_1_out, B);
  xor xor_2 (DIFFERENCE, xor_1_out, C);
  or or_1 (BORROW, and_1_out, and_2_out);

  // Notes on the sheet:
  //   not(A)
  //   FULL SUBSTRACTOR
  //   A xor B
  //   not(A xor B)
  //   not(A).B
  //   A xor B xor C
  //   (A xor B).C
endmodule
