// Logisim project PARALLEL ADDER.circ as structural Verilog: 1 circuit, main circuit main
module main (
  input  CONTROL,
  input  A0,
  input  B0,
  input  A1,
  input  B1,
  input  A2,
  input  B2,
  input  A3,
  input  B3,
  output S0,
  output S1,
  output S2,
  output S3,
  output CARRY
);

  wire adder_1_cout, adder_2_cout, adder_3_cout, xor_1_out, xor_2_out, xor_3_out, xor_4_out;

  xor xor_1 (xor_1_out, CONTROL, B0);
  xor xor_2 (xor_2_out, CONTROL, B1);
  xor xor_3 (xor_3_out, CONTROL, B2);
  xor xor_4 (xor_4_out, CONTROL, B3);
  Adder #(.width(1)) adder_1 (.a(A0), .b(xor_1_out), .out(S0), .cout(adder_1_cout));  // open: cin
  Adder #(.width(1)) adder_2 (.a(A1), .b(xor_2_out), .out(S1), .cin(adder_1_cout), .cout(adder_2_cout));
  Adder #(.width(1)) adder_3 (.a(A2), .b(xor_3_out), .out(S2), .cin(adder_2_cout), .cout(adder_3_cout));
  Adder #(.width(1)) adder_4 (.a(A3), .b(xor_4_out), .out(S3), .cin(adder_3_cout), .cout(CARRY));

  // Notes on the sheet:
  //   INPUT
  //   A3   A2   A1   A0:
  //   1     0     0     1
  //   B3   B2   B1   B0
  //   0     1     1      0
  //   (Cin)
  //   1 for subtract
  //   0 for Add
  //   B0 xor Cin
  //   B1 xor Cin
  //   B2 xor Cin
  //   B3 xor Cin
  //   PARALLEL ADDER
  //   OUTPUT
  //   S3    S2    S1    S0
  //   0      0      1      0
endmodule
