// Logisim project hardwired control signals.circ as structural Verilog: 1 circuit, main circuit main
module main (
  input  OP5,
  input  OP4,
  input  OP3,
  input  OP2,
  input  OP1,
  output out_6,
  output out_7,
  output out_8,
  output out_9,
  output out_10,
  output out_11
);

  wire and_1_out, and_2_out, and_3_out, not_1_out, not_2_out, not_3_out, not_4_out, not_5_out, or_1_out;

  not not_1 (not_1_out, OP5);
  not not_2 (not_2_out, OP4);
  not not_3 (not_3_out, OP3);
  not not_4 (not_4_out, OP2);
  not not_5 (not_5_out, OP1);
  and isSt (out_6, not_1_out, OP4, OP3, OP2, OP1);
  and isLd (out_7, not_1_out, OP2, OP3, OP4, not_5_out);
  and isBeq (out_8, OP5, not_2_out, not_3_out, not_4_out, not_5_out);
  and isBgt (out_9, OP5, not_2_out, not_3_out, not_4_out, OP1);
  and isRet (out_10, OP5, not_2_out, OP3, not_4_out, not_5_out);
  and and_1 (and_1_out, OP5, not_2_out);
  and and_2 (and_2_out, not_3_out, OP2);
  and and_3 (and_3_out, OP3, not_4_out, not_5_out);
  or or_1 (or_1_out, and_2_out, and_3_out);
  and isUbranch (out_11, and_1_out, or_1_out);

  // Notes on the sheet:
  //   HARDWIRED CONTROL SIGNALS
endmodule
